# Fritzing sketch WatchDoge (saved by Fritzing 0.9.3b)

parts:
  Part1 = Arduino Nano (Rev3.0)
  7_Segment_4_Digit_Display1 = 7-SEGMENT-4DIGIT common cathode [part_number=HS420561K-32 package=7-segment-4digit-cathode]
  R1 = Resistor [tolerance=±5% resistance=1k package=THT]
  R2 = Resistor [tolerance=±5% resistance=1k package=THT]
  R3 = Resistor [tolerance=±5% resistance=1k package=THT]
  R4 = Resistor [tolerance=±5% resistance=1k package=THT]
  R5 = Resistor [tolerance=±5% resistance=1k package=THT]
  R6 = Resistor [tolerance=±5% resistance=1k package=THT]
  R7 = Resistor [tolerance=±5% resistance=1k package=THT]
  R8 = Resistor [tolerance=±5% resistance=1k package=THT]

nets:
  N1: Part1.D4, 7_Segment_4_Digit_Display1.pin_12
  N2: Part1.D5, R2.Pin_1
  N3: Part1.D6, R3.Pin_1
  N4: Part1.D7, 7_Segment_4_Digit_Display1.pin_9
  N5: Part1.D8, 7_Segment_4_Digit_Display1.pin_8
  N6: Part1.D9, R1.Pin_1
  N7: Part1.A5, R4.Pin_0
  N8: Part1.A4, R5.Pin_0
  N9: Part1.A3, R6.Pin_0
  N10: Part1.A2, R7.Pin_0
  N11: Part1.A1, R8.Pin_0
  N12: Part1.A0, 7_Segment_4_Digit_Display1.pin_6
  N13: 7_Segment_4_Digit_Display1.pin_1, R4.Pin_1
  N14: 7_Segment_4_Digit_Display1.pin_2, R5.Pin_1
  N15: 7_Segment_4_Digit_Display1.pin_3, R6.Pin_1
  N16: 7_Segment_4_Digit_Display1.pin_4, R7.Pin_1
  N17: 7_Segment_4_Digit_Display1.pin_5, R8.Pin_1
  N18: 7_Segment_4_Digit_Display1.pin_7, R1.Pin_0
  N19: 7_Segment_4_Digit_Display1.pin_10, R3.Pin_0
  N20: 7_Segment_4_Digit_Display1.pin_11, R2.Pin_0

custom parts:
  7-SEGMENT-4DIGIT common cathode: A 7 Segment 4 Digit common cathode display, with decimal points
